# Fritzing sketch IR-blaster-perfboard (saved by Fritzing 0.9.3b)
circuit board: 4.05114cm x 2.23709cm
perfboards: 1

parts:
  R2 = Resistor [tolerance=±1% resistance=90 package=THT]
  R1 = Resistor [tolerance=±5% resistance=1k package=THT]
  V1 = DC Power [voltage=5]
  Q1 = NPN-Transistor [package="TO92 [THT]"]
  LED2 = LED - 5mm [color="Infrared (940nm)" current=50mA package="5 mm [THT]"]
  J2 = longpad pin header, 3 pins [form="long pad"]

nets:
  N1: R2.Pin_1, V1.V+, J2.pin3
  N2: R1.Pin_0, J2.pin2
  N3: R1.Pin_1, Q1.B
  N4: V1.V-, Q1.E, J2.pin1
  N5: Q1.C, LED2.cathode

notes:
  IR Blaster LS01
  GND
  GPIO
  +5V
  GND GPIO +5V
