# Fritzing sketch IR-blaster (saved by Fritzing 0.9.3b)
circuit board: 4.05114cm x 2.23709cm
breadboards: 1

parts:
  R2 = Resistor [tolerance=±5% resistance=100 package=THT]
  R1 = Resistor [tolerance=±5% resistance=1k package=THT]
  V1 = DC Power [voltage=5]
  WeMos_D1_Mini1 = WeMos D1 Mini
  Q1 = NPN-Transistor [package="TO92 [THT]"]
  LED1 = LED - 5mm [color="Infrared (940nm)" current=50mA package="5 mm [THT]"]
  J2 = longpad pin header, 3 pins [form="long pad"]

nets:
  N1: R2.Pin_0, LED1.anode
  N2: R2.Pin_1, V1.V+, J2.pin3
  N3: R1.Pin_0, WeMos_D1_Mini1.D7, J2.pin2
  N4: R1.Pin_1, Q1.B
  N5: V1.V-, Q1.E, J2.pin1
  N6: Q1.C, LED1.cathode

notes:
  IR Blaster LS01
  GND
  GPIO
  +5V
  GND GPIO +5V
